# Fritzing sketch Pi5_MCP3008_Potentiometer (saved by Fritzing 1.0.5)
breadboards: 1

parts:
  A8 = Raspberry Pi 5
  ADC1 = MCP3008 [package=dil16]
  R1 = Rotary Potentiometer (Large) [maximum_resistance=100kΩ knob_status=50% power=0.5W package=THT]

nets:
  3V3: A8.3V3, ADC1.VREF, ADC1.VDD, R1.leg1
  N1: A8.GPIO10, ADC1.Din
  N2: A8.GPIO9, ADC1.Dout
  N3: A8.GPIO11, ADC1.CLK
  N4: A8.GPIO8, ADC1.CS/SHDN
  N5: ADC1.CH0, R1.wiper
  N6: ADC1.DGND, ADC1.AGND, R1.leg2

custom parts:
  Raspberry Pi 5: The RPi5, a faster version of the awesome Raspberry Pi4B ARM Board with 40 pin gpio.
