# Fritzing sketch RaspberryPiRoomCondition (saved by Fritzing 0.9.7b)

parts:
  Part1 = SCD30
  MCU1 = Raspberry Pi Zero
  IC1 = 2.8 inch LCD SPI display with touch screen & SD card

nets:
  N1: Part1.VDD, MCU1.pin_1, MCU1.pin_17, IC1.pin8
  N2: Part1.GND, MCU1.pin_6, MCU1.pin_9, MCU1.pin_25, MCU1.pin_30, IC1.pin2
  N3: Part1.TX/SCL, MCU1.pin_5
  N4: Part1.RX/SDA, MCU1.pin_3
  N5: MCU1.pin_2, IC1.pin1
  N6: MCU1.pin_18, IC1.pin4
  N7: MCU1.pin_19, IC1.pin6
  N8: MCU1.pin_21, IC1.pin_9
  N9: MCU1.pin_22, IC1.pin5
  N10: MCU1.pin_23, IC1.pin7
  N11: MCU1.pin_24, IC1.pin3

custom parts:
  SCD30: CO2 , humidity, and temperature sensor * Current consumption: 19 mA @ 1 meas. per 2 s. * Digital interface UART or I2C * Company: Sensirion - The Sensor Company Electrical specifications * average current: 19 mA * max. current: 75 mA * DC supply: 3.3 V - 5.5 V Operation conditions * temperature: 0 – 50°C * humidity: 0 – 95 %RH * sensor lifetime: 15 years CO2-sensor: * NDIR CO 2 sensor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
  2.8 inch LCD SPI display with touch screen & SD card: A generic 2.8 inch LCD TFT 320x280 display with touchscreen and SD card slot.
